// Logisim project 实验电路.circ as structural Verilog
module \实验一  (
  input  in_1
);

  wire clock_1_out, \实验一译码器_1_a , \实验一译码器_1_b , \实验一译码器_1_c , \实验一译码器_1_d , \实验一译码器_1_e , \实验一译码器_1_f ,
       \实验一译码器_1_g ;
  wire [3:0] counter_1_q;

  Counter #(.width(4), .max('hf), .ongoal("wrap"), .trigger("rising"), .behavior("new")) counter_1 (
    .Q(counter_1_q), .clk(clock_1_out));  // open: load, D, count, carry, clr, preset, down
  Clock #(.highDuration(1), .lowDuration(1)) clock_1 (.out(clock_1_out));
  \实验一译码器  \u_实验一译码器_1  (
    .A0(counter_1_q[0]), .A1(counter_1_q[1]), .A2(counter_1_q[2]), .A3(counter_1_q[3]), .Y(in_1),
    .a(\实验一译码器_1_a ), .b(\实验一译码器_1_b ), .c(\实验一译码器_1_c ), .d(\实验一译码器_1_d ), .e(\实验一译码器_1_e ),
    .f(\实验一译码器_1_f ), .g(\实验一译码器_1_g ));
  _7_Segment_Display #(.active("true")) u_7_segment_display_1 (
    .g(\实验一译码器_1_g ), .f(\实验一译码器_1_f ), .a(\实验一译码器_1_a ), .b(\实验一译码器_1_b ), .e(\实验一译码器_1_e ),
    .d(\实验一译码器_1_d ), .c(\实验一译码器_1_c ));  // open: dp
endmodule

module \实验二  (
  input  [7:0] A,
  input  [7:0] B,
  input  [7:0] in_3,
  output [15:0] result
);

  wire clock, clock_1_out, comparator_1_eq, comparator_2_eq, done, LA, LB, LP, not_1_out, not_2_out, reset,
       SA, SB, start;
  wire [7:0] multiplexer_2_out, register_3_q, shifter_2_out;
  wire [15:0] adder_1_out, bit_extender_1_out, multiplexer_1_out, register_1_q, shifter_1_out;

  Multiplexer #(.select(1), .width(16), .disabled("Z"), .enable("false")) multiplexer_1 (
    .in0(bit_extender_1_out), .in1(shifter_1_out), .out(multiplexer_1_out), .sel(SA));
  Clock #(.highDuration(1), .lowDuration(1)) clock_1 (.out(clock_1_out));
  // DipSwitch #(.NSwitches(1)) dipswitch_1: pin names not known; wires that end beside it: start
  Button button_1 (.out(reset));
  assign bit_extender_1_out = {{8{1'b0}}, A};  // Bit_Extender bit_extender_1
  Register #(.width(16), .trigger("rising"), .Select("low")) register_1 (
    .D(multiplexer_1_out), .en(LA), .Q(register_1_q), .clk(clock), .clr(reset));
  Register #(.width(16), .trigger("rising"), .Select("low")) register_2 (
    .D(adder_1_out), .en(LP), .Q(result), .clk(clock), .clr(reset));
  not not_1 (not_1_out, done);
  Shifter #(.width(16), .shift("ll")) shifter_1 (.in(register_1_q), .\dist (4'b0001), .out(shifter_1_out));
  Adder #(.width(16)) adder_1 (.a(register_1_q), .b(result), .out(adder_1_out));  // open: cin, cout
  and and_1 (clock, not_1_out, clock_1_out);
  Multiplexer #(.select(1), .width(8), .disabled("Z"), .enable("false")) multiplexer_2 (
    .in0(B), .in1(shifter_2_out), .out(multiplexer_2_out), .sel(SB));
  Register #(.width(8), .trigger("rising"), .Select("low")) register_3 (
    .D(multiplexer_2_out), .en(LB), .Q(register_3_q), .clk(clock), .clr(reset));
  Comparator #(.width(8), .mode("twosComplement")) comparator_1 (
    .a(register_3_q), .b(in_3), .eq(comparator_1_eq));  // open: gt, lt
  Shifter #(.width(8), .shift("lr")) shifter_2 (.in(register_3_q), .\dist (3'b001), .out(shifter_2_out));
  not not_2 (not_2_out, comparator_1_eq);
  Comparator #(.width(1), .mode("twosComplement")) comparator_2 (
    .a(register_3_q[0]), .b(1'b1), .eq(comparator_2_eq));  // open: gt, lt
  \实验二FSM  \u_实验二fsm_1  (
    .start(start), .B(not_2_out), .B0(comparator_2_eq), .clock(clock), .reset(reset), .LA(LA), .SA(SA),
    .LB(LB), .SB(SB), .LP(LP), .done(done));
endmodule

module \实验三  (
);

  wire ALUSrc, and_1_out, Branch, clear, CLK, clock_1_out, isBne, MemtoReg, MemWrite, multiplexer_2_out,
       not_1_out, RegDst, RegWrite, Syscall, \实验三alu_1_zero ;
  wire [2:0] ALUControl;
  wire [4:0] multiplexer_3_out;
  wire [5:0] funct, op;
  wire [25:6] \实验三rom_1_data_bus_out ;
  wire [31:0] adder_1_out, adder_2_out, bit_extender_1_out, multiplexer_1_out, multiplexer_4_out,
       multiplexer_5_out, PC_q, shifter_1_out, \实验三alu_1_result , \实验三ram_1_data_bus_out ,
       \实验三寄存器文件的封装_1_rd1 , \实验三寄存器文件的封装_1_rd2 ;

  Register #(.width(32), .trigger("rising"), .Select("low")) PC (
    .D(multiplexer_1_out), .Q(PC_q), .clk(CLK));  // open: en, clr
  Multiplexer #(.select(1), .width(32), .disabled("Z"), .enable("false")) multiplexer_1 (
    .in0(adder_1_out), .in1(adder_2_out), .out(multiplexer_1_out), .sel(multiplexer_2_out));
  Adder #(.width(32)) adder_1 (.a(PC_q), .b(32'h4), .out(adder_1_out));  // open: cin, cout
  \实验三ROM  \u_实验三rom_1  (.CS(1'b1), .Address_Bus(PC_q), .Data_Bus_Out({op, \实验三rom_1_data_bus_out , funct}));
  Clock #(.highDuration(1), .lowDuration(1)) clock_1 (.out(clock_1_out));
  or or_1 (CLK, clock_1_out, Syscall);
  Button button_1 (.out(clear));
  \实验三寄存器文件的封装  \u_实验三寄存器文件的封装_1  (
    .A1(\实验三rom_1_data_bus_out [25:21]), .A2(\实验三rom_1_data_bus_out [20:16]), .A3(multiplexer_3_out),
    .WD3(multiplexer_5_out), .RD1(\实验三寄存器文件的封装_1_rd1 ), .RD2(\实验三寄存器文件的封装_1_rd2 ), .CLK(CLK), .WE3(RegWrite));
  assign bit_extender_1_out = {{16{\实验三rom_1_data_bus_out [15]}}, {\实验三rom_1_data_bus_out [15:6], funct}};  // Bit_Extender bit_extender_1
  Multiplexer #(.select(1), .width(1), .disabled("Z"), .enable("false")) multiplexer_2 (
    .in0(and_1_out), .in1(not_1_out), .out(multiplexer_2_out), .sel(isBne));
  Multiplexer #(.select(1), .width(5), .disabled("Z"), .enable("false")) multiplexer_3 (
    .in0(\实验三rom_1_data_bus_out [20:16]), .in1(\实验三rom_1_data_bus_out [15:11]), .out(multiplexer_3_out),
    .sel(RegDst));
  not not_1 (not_1_out, and_1_out);
  Multiplexer #(.select(1), .width(32), .disabled("Z"), .enable("false")) multiplexer_4 (
    .in0(\实验三寄存器文件的封装_1_rd2 ), .in1(bit_extender_1_out), .out(multiplexer_4_out), .sel(ALUSrc));
  Shifter #(.width(32), .shift("ll")) shifter_1 (.in(bit_extender_1_out), .\dist (5'b00010), .out(shifter_1_out));
  \实验三ALU  \u_实验三alu_1  (
    .A(\实验三寄存器文件的封装_1_rd1 ), .B(multiplexer_4_out), .Zero(\实验三alu_1_zero ), .Result(\实验三alu_1_result ),
    .F(ALUControl));
  Adder #(.width(32)) adder_2 (.a(shifter_1_out), .b(adder_1_out), .out(adder_2_out));  // open: cin, cout
  \实验三控制单元  \u_实验三控制单元_1  (
    .opcode(op), .funct(funct), .RegWrite(RegWrite), .RegDst(RegDst), .ALUSrc(ALUSrc), .Branch(Branch),
    .MemWrite(MemWrite), .MemtoReg(MemtoReg), .isBne(isBne), .ALUControl(ALUControl), .Syscall(Syscall));
  and and_1 (and_1_out, Branch, \实验三alu_1_zero );
  \实验三RAM  \u_实验三ram_1  (
    .CS(1'b1), .Store(MemWrite), .CLK(CLK), .Address_Bus(\实验三alu_1_result ),
    .Data_Bus_In(\实验三寄存器文件的封装_1_rd2 ), .Load(1'b1), .Clear(clear), .Data_Bus_Out(\实验三ram_1_data_bus_out ));
  Multiplexer #(.select(1), .width(32), .disabled("Z"), .enable("false")) multiplexer_5 (
    .in0(\实验三alu_1_result ), .in1(\实验三ram_1_data_bus_out ), .out(multiplexer_5_out), .sel(MemtoReg));
endmodule

module \_4位无符号加法器  (
  input  A1,
  input  B1,
  input  A2,
  input  B2,
  input  A3,
  input  B3,
  input  A3_2,
  input  B3_2,
  output R,
  output C,
  output R_2,
  output C_2,
  output R_3,
  output C_3,
  output R_4,
  output Y
);

  wire and_1_out, and_2_out, and_3_out, and_4_out, and_5_out, and_6_out, and_7_out, and_8_out, and_9_out,
       nand_1_out;

  xor xor_1 (R, A1, B1);
  nand nand_1 (nand_1_out, B1, A1);
  xor xor_2 (R_2, A2, C, B2);
  and and_1 (and_1_out, B2, A2);
  and and_2 (and_2_out, C, A2);
  and and_3 (and_3_out, C, B2);
  xor xor_3 (R_3, A3, C_2, B3);
  and and_4 (and_4_out, B3, A3);
  and and_5 (and_5_out, C_2, A3);
  and and_6 (and_6_out, C_2, B3);
  xor xor_4 (R_4, A3_2, C_3, B3_2);
  and and_7 (and_7_out, B3_2, A3_2);
  and and_8 (and_8_out, C_3, A3_2);
  and and_9 (and_9_out, C_3, B3_2);
  not not_1 (C, nand_1_out);
  or or_1 (C_2, and_1_out, and_2_out, and_3_out);
  or or_2 (C_3, and_4_out, and_5_out, and_6_out);
  or or_3 (Y, and_7_out, and_8_out, and_9_out);
endmodule

module \_4位有符号加法器  (
  input  A1,
  input  B1,
  input  A2,
  input  B2,
  input  A3,
  input  B3,
  input  A3_2,
  input  B3_2,
  output R,
  output C,
  output R_2,
  output C_2,
  output R_3,
  output C_3,
  output R_4,
  output Y
);

  wire and_1_out, and_2_out, and_3_out, and_4_out, and_5_out, and_6_out, and_7_out, and_8_out, nand_1_out,
       not_1_out, not_2_out, not_3_out;

  xor xor_1 (R, A1, B1);
  nand nand_1 (nand_1_out, B1, A1);
  xor xor_2 (R_2, A2, C, B2);
  and and_1 (and_1_out, B2, A2);
  and and_2 (and_2_out, C, A2);
  and and_3 (and_3_out, C, B2);
  xor xor_3 (R_3, A3, C_2, B3);
  and and_4 (and_4_out, B3, A3);
  and and_5 (and_5_out, C_2, A3);
  and and_6 (and_6_out, C_2, B3);
  xor xor_4 (R_4, A3_2, C_3, B3_2);
  not not_1 (not_1_out, A3_2);
  not not_2 (not_2_out, B3_2);
  not not_3 (not_3_out, C_3);
  not not_4 (C, nand_1_out);
  or or_1 (C_2, and_1_out, and_2_out, and_3_out);
  or or_2 (C_3, and_4_out, and_5_out, and_6_out);
  and and_7 (and_7_out, not_1_out, not_2_out, C_3);
  and and_8 (and_8_out, B3_2, A3_2, not_3_out);
  or or_3 (Y, and_7_out, and_8_out);
endmodule

module \轨道信号灯  (
  input  \第三段轨道 ,
  input  \自身所处轨道 ,
  input  \黄灯信号或第二段轨道 ,
  output out_4,
  output \红灯信号 ,
  output \黄灯信号 
);

  wire not_1_out;

  not not_1 (not_1_out, \黄灯信号或第二段轨道 );
  and and_1 (\红灯信号 , \自身所处轨道 , \黄灯信号或第二段轨道 );
  and and_2 (\黄灯信号 , \第三段轨道 , \自身所处轨道 , not_1_out);
  nor nor_1 (out_4, \黄灯信号 , \红灯信号 );
endmodule

module \交通灯  (
);

  wire clock_1_out, demultiplexer_1_out0, demultiplexer_1_out1, demultiplexer_1_out2, demultiplexer_2_out0,
       demultiplexer_2_out1, demultiplexer_2_out2, reset, TA, TB;
  wire [1:0] LA, LB;

  Button button_1 (.out(reset));
  Button button_2 (.out(TA));
  Button button_3 (.out(TB));
  \交通灯FSM  \u_交通灯fsm_1  ();
  Clock #(.highDuration(1), .lowDuration(1)) clock_1 (.out(clock_1_out));
  Demultiplexer #(.select(2), .width(1), .tristate("false"), .disabled("Z"), .enable("false")) demultiplexer_1 (
    .out0(demultiplexer_1_out0), .out1(demultiplexer_1_out1), .out2(demultiplexer_1_out2), .in(1'b1), .sel(LA));  // open: out3
  Demultiplexer #(.select(2), .width(1), .tristate("false"), .disabled("Z"), .enable("false")) demultiplexer_2 (
    .out0(demultiplexer_2_out0), .out1(demultiplexer_2_out1), .out2(demultiplexer_2_out2), .in(1'b1), .sel(LB));  // open: out3
  LED #(.active("true")) led_1 (.in(demultiplexer_1_out0));
  LED #(.active("true")) led_2 (.in(demultiplexer_1_out1));
  LED #(.active("true")) led_3 (.in(demultiplexer_1_out2));
  LED #(.active("true")) led_4 (.in(demultiplexer_2_out0));
  LED #(.active("true")) led_5 (.in(demultiplexer_2_out1));
  LED #(.active("true")) led_6 (.in(demultiplexer_2_out2));

  // Notes on the sheet:
  //   横向交通灯
  //   纵向交通灯
endmodule

module \交通灯FSM状态选择  (
  input  S1,
  input  S0,
  input  TA,
  input  TB,
  output S11,
  output S00
);

  wire and_1_out, and_2_out, and_3_out, and_4_out, not_1_out, not_2_out, not_3_out, not_4_out, not_5_out,
       not_6_out, not_7_out;

  not not_1 (not_1_out, S1);
  not not_2 (not_2_out, S0);
  not not_3 (not_3_out, S1);
  not not_4 (not_4_out, S0);
  not not_5 (not_5_out, TA);
  not not_6 (not_6_out, S0);
  not not_7 (not_7_out, TB);
  and and_1 (and_1_out, not_1_out, S0);
  or or_1 (S11, and_1_out, and_2_out);
  and and_2 (and_2_out, S1, not_2_out);
  and and_3 (and_3_out, not_3_out, not_4_out, not_5_out);
  or or_2 (S00, and_3_out, and_4_out);
  and and_4 (and_4_out, S1, not_6_out, not_7_out);
endmodule

module \交通灯FSM输出部分  (
  input  S1,
  input  S0,
  output LA1,
  output LA0,
  output LB1,
  output LB0
);

  wire not_1_out;

  not not_1 (not_1_out, S1);
  not not_2 (LB1, S1);
  and and_1 (LB0, S1, S0);
  and and_2 (LA0, not_1_out, S0);

  assign LA1 = S1;
endmodule

module \交通灯FSM状态选择的封装  (
  input  CLK,
  input  RESET,
  input  TA,
  input  TB,
  output S1,
  output S0
);

  wire [1:0] \交通灯fsm状态选择_1_s00 ;

  \交通灯FSM状态选择  \u_交通灯fsm状态选择_1  (
    .S1(S1), .S0(S0), .TA(TA), .TB(TB), .S11(\交通灯fsm状态选择_1_s00 [1]), .S00(\交通灯fsm状态选择_1_s00 [0]));
  Register #(.width(2), .trigger("rising"), .Select("low")) register_1 (
    .D(\交通灯fsm状态选择_1_s00 ), .Q({S1, S0}), .clk(CLK), .clr(RESET));  // open: en
endmodule

module \存储系统的设计  (
  input  [11:0] adress,
  input  RE,
  output [7:0] data
);

  wire [3:0] ram_1_data, ram_2_data, ram_3_data, ram_4_data, ram_5_data, ram_6_data, ram_7_data, ram_8_data;

  RAM #(.addrWidth(10), .dataWidth(4), .bus("combined"), .Select("low")) ram_1 (
    .addr(adress[11:2]), .data(ram_1_data), .ld(RE));  // open: sel, clk, clr
  RAM #(.addrWidth(10), .dataWidth(4), .bus("combined"), .Select("low")) ram_2 (
    .addr(adress[11:2]), .data(ram_2_data), .ld(RE));  // open: sel, clk, clr
  RAM #(.addrWidth(10), .dataWidth(4), .bus("combined"), .Select("low")) ram_3 (
    .addr(adress[11:2]), .data(ram_3_data), .ld(RE));  // open: sel, clk, clr
  RAM #(.addrWidth(10), .dataWidth(4), .bus("combined"), .Select("low")) ram_4 (
    .addr(adress[11:2]), .data(ram_4_data), .ld(RE));  // open: sel, clk, clr
  RAM #(.addrWidth(10), .dataWidth(4), .bus("combined"), .Select("low")) ram_5 (
    .addr(adress[11:2]), .data(ram_5_data), .ld(RE));  // open: sel, clk, clr
  RAM #(.addrWidth(10), .dataWidth(4), .bus("combined"), .Select("low")) ram_6 (
    .addr(adress[11:2]), .data(ram_6_data), .ld(RE));  // open: sel, clk, clr
  RAM #(.addrWidth(10), .dataWidth(4), .bus("combined"), .Select("low")) ram_7 (
    .addr(adress[11:2]), .data(ram_7_data), .ld(RE));  // open: sel, clk, clr
  RAM #(.addrWidth(10), .dataWidth(4), .bus("combined"), .Select("low")) ram_8 (
    .addr(adress[11:2]), .data(ram_8_data), .ld(RE));  // open: sel, clk, clr
  Multiplexer #(.select(2), .width(8), .disabled("Z"), .enable("false")) multiplexer_1 (
    .in0({ram_2_data, ram_1_data}), .in1({ram_4_data, ram_3_data}), .in2({ram_6_data, ram_5_data}),
    .in3({ram_8_data, ram_7_data}), .out(data), .sel(adress[1:0]));

  // Notes on the sheet:
  //   8片1k*4位存储器组成4k*8位存储器
endmodule

module \实验一译码器  (
  input  A0,
  input  A1,
  input  A2,
  input  A3,
  input  Y,
  output a,
  output b,
  output c,
  output d,
  output e,
  output f,
  output g
);

  wire and_1_out, and_2_out, and_3_out, and_4_out, and_5_out, and_6_out, and_7_out, and_8_out, and_9_out,
       and_10_out, and_11_out, and_12_out, and_13_out, and_14_out, and_15_out, and_16_out, and_17_out,
       and_18_out, and_19_out, and_20_out, and_21_out, and_22_out, and_23_out, and_24_out, and_25_out,
       and_26_out, and_27_out, and_28_out, and_29_out, and_30_out, and_31_out, and_32_out, and_33_out,
       and_34_out, and_35_out, not_1_out, not_2_out, not_3_out, not_4_out, not_5_out, not_6_out, not_7_out,
       not_8_out, not_9_out, not_10_out, not_11_out, not_12_out, not_13_out, not_14_out, not_15_out,
       not_16_out, not_17_out, not_18_out, not_19_out, not_20_out, not_21_out, not_22_out, not_23_out,
       not_24_out, not_25_out, not_26_out, not_27_out, not_28_out, not_29_out, not_30_out, not_31_out,
       not_32_out, not_33_out, not_34_out, not_35_out, not_36_out, not_37_out, not_38_out, not_39_out,
       not_40_out, not_41_out, not_42_out, not_43_out, or_1_out, or_2_out, or_3_out, or_4_out, or_5_out,
       or_6_out, or_7_out;

  not not_1 (not_1_out, A2);
  and and_1 (and_1_out, not_1_out, not_2_out);
  not not_2 (not_2_out, A0);
  not not_3 (not_3_out, A3);
  and and_2 (and_2_out, not_3_out, A1);
  not not_4 (not_4_out, A3);
  and and_3 (and_3_out, not_4_out, A2, A0);
  and and_4 (and_4_out, A2, A1);
  and and_5 (and_5_out, A3, not_5_out, not_6_out);
  not not_5 (not_5_out, A2);
  not not_6 (not_6_out, A1);
  and and_6 (and_6_out, A3, not_7_out);
  not not_7 (not_7_out, A0);
  not not_8 (not_8_out, A3);
  and and_7 (and_7_out, not_8_out, not_9_out);
  not not_9 (not_9_out, A2);
  not not_10 (not_10_out, A3);
  and and_8 (and_8_out, not_10_out, not_11_out, not_12_out);
  not not_11 (not_11_out, A1);
  not not_12 (not_12_out, A0);
  not not_13 (not_13_out, A2);
  and and_9 (and_9_out, not_13_out, not_14_out);
  not not_14 (not_14_out, A0);
  not not_15 (not_15_out, A3);
  and and_10 (and_10_out, not_15_out, A1, A0);
  and and_11 (and_11_out, A3, not_16_out, A0);
  not not_16 (not_16_out, A1);
  not not_17 (not_17_out, A3);
  and and_12 (and_12_out, not_17_out, not_18_out);
  not not_18 (not_18_out, A1);
  not not_19 (not_19_out, A3);
  and and_13 (and_13_out, not_19_out, A0);
  not not_20 (not_20_out, A1);
  and and_14 (and_14_out, not_20_out, A0);
  not not_21 (not_21_out, A3);
  and and_15 (and_15_out, not_21_out, A2);
  and and_16 (and_16_out, A3, not_22_out);
  not not_22 (not_22_out, A2);
  not not_23 (not_23_out, A3);
  not not_24 (not_24_out, A2);
  and and_17 (and_17_out, not_23_out, not_24_out, not_25_out);
  not not_25 (not_25_out, A0);
  not not_26 (not_26_out, A2);
  and and_18 (and_18_out, not_26_out, A1, A0);
  not not_27 (not_27_out, A1);
  and and_19 (and_19_out, A2, not_27_out, A0);
  and and_20 (and_20_out, A2, A1, not_28_out);
  not not_28 (not_28_out, A0);
  and and_21 (and_21_out, A3, not_29_out);
  not not_29 (not_29_out, A1);
  not not_30 (not_30_out, A2);
  and and_22 (and_22_out, not_30_out, not_31_out);
  not not_31 (not_31_out, A0);
  and and_23 (and_23_out, A1, not_32_out);
  not not_32 (not_32_out, A0);
  and and_24 (and_24_out, A3, A1);
  and and_25 (and_25_out, A3, A2);
  not not_33 (not_33_out, A1);
  and and_26 (and_26_out, not_33_out, not_34_out);
  not not_34 (not_34_out, A0);
  not not_35 (not_35_out, A3);
  and and_27 (and_27_out, not_35_out, A2, not_36_out);
  not not_36 (not_36_out, A1);
  and and_28 (and_28_out, A2, not_37_out);
  not not_37 (not_37_out, A0);
  and and_29 (and_29_out, A3, not_38_out);
  not not_38 (not_38_out, A2);
  and and_30 (and_30_out, A3, A1);
  not not_39 (not_39_out, A2);
  and and_31 (and_31_out, not_39_out, A1);
  and and_32 (and_32_out, A1, not_40_out);
  not not_40 (not_40_out, A0);
  not not_41 (not_41_out, A3);
  and and_33 (and_33_out, not_41_out, A2, not_42_out);
  not not_42 (not_42_out, A1);
  and and_34 (and_34_out, A3, not_43_out);
  not not_43 (not_43_out, A2);
  and and_35 (and_35_out, A3, A0);
  or or_1 (or_1_out, and_7_out, and_8_out, and_9_out, and_10_out, and_11_out);
  or or_2 (or_2_out, and_12_out, and_13_out, and_14_out, and_15_out, and_16_out);
  or or_3 (or_3_out, and_17_out, and_18_out, and_19_out, and_20_out, and_21_out);
  or or_4 (or_4_out, and_22_out, and_23_out, and_24_out, and_25_out);
  or or_5 (or_5_out, and_26_out, and_27_out, and_28_out, and_29_out, and_30_out);
  or or_6 (or_6_out, and_31_out, and_32_out, and_33_out, and_34_out, and_35_out);
  or or_7 (or_7_out, and_1_out, and_2_out, and_3_out, and_4_out, and_5_out, and_6_out);
  xor xor_1 (a, or_7_out, Y);
  xor xor_2 (b, or_1_out, Y);
  xor xor_3 (c, or_2_out, Y);
  xor xor_4 (d, or_3_out, Y);
  xor xor_5 (e, or_4_out, Y);
  xor xor_6 (f, or_5_out, Y);
  xor xor_7 (g, or_6_out, Y);
endmodule

module \实验二FSM输出部分  (
  input  S2,
  input  S1,
  input  S0,
  output LA,
  output SA,
  output LB,
  output SB,
  output LP,
  output DONE
);

  wire and_2_out, and_3_out, not_1_out, not_2_out, not_3_out, not_4_out;

  not not_1 (not_1_out, S2);
  not not_2 (not_2_out, S0);
  not not_3 (not_3_out, S2);
  not not_4 (not_4_out, S0);
  and and_1 (LP, S1, S0);
  and and_2 (and_2_out, not_1_out, not_2_out);
  and and_3 (and_3_out, not_3_out, not_4_out);
  or or_1 (LA, and_2_out, S1);
  or or_2 (LB, and_3_out, S1);

  assign DONE = S2;
  assign SA = S1;
  assign SB = S1;
endmodule

module \实验二FSM状态选择  (
  input  clock,
  input  reset,
  input  start,
  input  B,
  input  B0,
  output S2,
  output S1,
  output S0
);

  wire [2:0] \实验二fsm状态选择的内置电路_1_s22 ;

  \实验二FSM状态选择的内置电路  \u_实验二fsm状态选择的内置电路_1  (
    .S2(S2), .S1(S1), .S0(S0), .start(start), .B(B), .B0(B0), .S22(\实验二fsm状态选择的内置电路_1_s22 [0]),
    .S12(\实验二fsm状态选择的内置电路_1_s22 [1]), .S02(\实验二fsm状态选择的内置电路_1_s22 [2]));
  Register #(.width(3), .trigger("rising"), .Select("low")) register_1 (
    .D(\实验二fsm状态选择的内置电路_1_s22 ), .Q({S0, S1, S2}), .clk(clock), .clr(reset));  // open: en
endmodule

module \实验二FSM状态选择的内置电路  (
  input  S2,
  input  S1,
  input  S0,
  input  start,
  input  B,
  input  B0,
  output S22,
  output S12,
  output S02
);

  wire and_1_out, and_2_out, and_3_out, and_4_out, and_5_out, and_6_out, not_1_out, not_2_out, not_3_out,
       not_4_out, not_5_out, not_6_out, not_7_out;

  not not_1 (not_1_out, S1);
  not not_2 (not_2_out, B);
  not not_3 (not_3_out, S1);
  not not_4 (not_4_out, S2);
  not not_5 (not_5_out, S0);
  not not_6 (not_6_out, S2);
  not not_7 (not_7_out, S2);
  and and_1 (and_1_out, not_1_out, S0, not_2_out);
  and and_2 (and_2_out, not_3_out, S0, B);
  and and_3 (and_3_out, S2, S1, B);
  and and_4 (and_4_out, not_4_out, not_5_out, start);
  and and_5 (and_5_out, not_6_out, start, B, B0);
  and and_6 (and_6_out, not_7_out, S1);
  or or_1 (S22, and_1_out, S2);
  or or_2 (S12, and_2_out, and_3_out);
  or or_3 (S02, and_4_out, and_5_out, and_6_out);
endmodule

module \实验二FSM  (
  input  start,
  input  B,
  input  B0,
  input  clock,
  input  reset,
  output LA,
  output SA,
  output LB,
  output SB,
  output LP,
  output done
);

  wire \实验二fsm状态选择_1_s0 , \实验二fsm状态选择_1_s1 , \实验二fsm状态选择_1_s2 ;

  \实验二FSM状态选择  \u_实验二fsm状态选择_1  (
    .start(start), .B(B), .B0(B0), .clock(clock), .reset(reset), .S2(\实验二fsm状态选择_1_s2 ),
    .S1(\实验二fsm状态选择_1_s1 ), .S0(\实验二fsm状态选择_1_s0 ));
  \实验二FSM输出部分  \u_实验二fsm输出部分_1  (
    .S2(\实验二fsm状态选择_1_s2 ), .S1(\实验二fsm状态选择_1_s1 ), .S0(\实验二fsm状态选择_1_s0 ), .LA(LA), .SA(SA), .LB(LB),
    .SB(SB), .LP(LP), .DONE(done));
endmodule

module \实验三ALU  (
  input  [2:0] F,
  input  [31:0] A,
  input  [31:0] B,
  output Zero,
  output [31:0] Result
);

  wire adder_1_cout, comparator_1_lt;
  wire [31:0] adder_1_out, and_1_out, bit_extender_1_out, multiplexer_1_out, not_1_out, or_1_out;

  assign not_1_out = ~B;  // NOT_Gate not_1, 32 bits wide
  Multiplexer #(.select(1), .width(32), .disabled("Z"), .enable("false")) multiplexer_1 (
    .in0(B), .in1(not_1_out), .out(multiplexer_1_out), .sel(F[2]));
  Comparator #(.width(32), .mode("twosComplement")) comparator_1 (.a(A), .b(B), .lt(comparator_1_lt));  // open: gt, eq
  Comparator #(.width(32), .mode("twosComplement")) comparator_2 (.a(A), .b(B), .eq(Zero));  // open: gt, lt
  assign and_1_out = multiplexer_1_out & A;  // AND_Gate and_1, 32 bits wide
  assign or_1_out = multiplexer_1_out | A;  // OR_Gate or_1, 32 bits wide
  Adder #(.width(32)) adder_1 (.a(multiplexer_1_out), .b(A), .out(adder_1_out), .cout(adder_1_cout));  // open: cin
  assign bit_extender_1_out = {{31{1'b0}}, comparator_1_lt};  // Bit_Extender bit_extender_1
  Multiplexer #(.select(2), .width(32), .disabled("Z"), .enable("false")) multiplexer_2 (
    .in0(and_1_out), .in1(or_1_out), .in2(adder_1_out), .in3(bit_extender_1_out), .out(Result), .sel(F[1:0]));
  // also tied to GND on the sheet: adder_1_cout
endmodule

module \实验三ALU译码器的内部电路  (
  input  ALUOp1,
  input  ALUOp0,
  input  F3,
  input  F2,
  input  F1,
  input  F0,
  output ALUControl2,
  output ALUControl1,
  output ALUControl0
);

  wire and_1_out, and_2_out, and_3_out, and_4_out, and_5_out, not_1_out, not_2_out, not_3_out;

  and and_1 (and_1_out, ALUOp1, F1);
  and and_2 (and_2_out, ALUOp1, ALUOp0);
  not not_1 (not_1_out, ALUOp1);
  not not_2 (not_2_out, F2);
  not not_3 (not_3_out, ALUOp1);
  or or_1 (ALUControl2, and_1_out, and_2_out);
  or or_2 (ALUControl1, not_1_out, not_2_out);
  and and_3 (and_3_out, not_3_out, ALUOp0);
  and and_4 (and_4_out, ALUOp1, F0);
  and and_5 (and_5_out, ALUOp1, F3);
  or or_3 (ALUControl0, and_3_out, and_4_out, and_5_out);
endmodule

module \实验三ALU译码器  (
  input  [1:0] ALUOp,
  input  [5:0] Funct,
  output [2:0] ALUControl
);

  \实验三ALU译码器的内部电路  \u_实验三alu译码器的内部电路_1  (
    .ALUOp1(ALUOp[1]), .ALUOp0(ALUOp[0]), .F3(Funct[3]), .F2(Funct[2]), .F1(Funct[1]), .F0(Funct[0]),
    .ALUControl2(ALUControl[2]), .ALUControl1(ALUControl[1]), .ALUControl0(ALUControl[0]));
endmodule

module \实验三控制单元的主译码器  (
  input  Opcode5,
  input  Opcode4,
  input  Opcode3,
  input  Opcode2,
  input  Opcode1,
  input  Opcode0,
  output RegWrite,
  output RegDst,
  output ALUSrc,
  output Branch,
  output MemWrite,
  output MemtoReg,
  output [1:0] ALUOp,
  output isBne
);

  wire and_1_out, and_2_out, and_3_out, and_4_out, and_5_out, and_6_out, and_7_out, and_8_out, and_10_out,
       and_11_out, and_12_out, and_13_out, and_14_out, and_15_out, and_16_out, and_17_out, and_18_out,
       not_1_out, not_2_out, not_3_out, not_4_out, not_5_out, not_6_out, not_7_out, not_8_out, not_9_out,
       not_10_out, not_11_out, not_12_out, not_13_out, not_14_out, not_15_out, not_16_out, not_17_out,
       not_18_out, not_19_out, not_20_out, not_21_out, not_22_out, not_23_out, not_24_out, not_25_out,
       not_26_out, not_27_out, not_28_out, not_29_out, not_30_out, not_31_out, not_32_out, not_33_out,
       not_34_out;

  not not_1 (not_1_out, Opcode5);
  not not_2 (not_2_out, Opcode4);
  not not_3 (not_3_out, Opcode2);
  not not_4 (not_4_out, Opcode1);
  not not_5 (not_5_out, Opcode0);
  not not_6 (not_6_out, Opcode3);
  not not_7 (not_7_out, Opcode2);
  not not_8 (not_8_out, Opcode3);
  not not_9 (not_9_out, Opcode1);
  not not_10 (not_10_out, Opcode1);
  not not_11 (not_11_out, Opcode1);
  not not_12 (not_12_out, Opcode1);
  not not_13 (not_13_out, Opcode1);
  not not_14 (not_14_out, Opcode5);
  not not_15 (not_15_out, Opcode4);
  not not_16 (not_16_out, Opcode2);
  not not_17 (not_17_out, Opcode0);
  not not_18 (not_18_out, Opcode3);
  not not_19 (not_19_out, Opcode2);
  not not_20 (not_20_out, Opcode2);
  not not_21 (not_21_out, Opcode2);
  not not_22 (not_22_out, Opcode2);
  not not_23 (not_23_out, Opcode3);
  not not_24 (not_24_out, Opcode2);
  not not_25 (not_25_out, Opcode1);
  not not_26 (not_26_out, Opcode2);
  not not_27 (not_27_out, Opcode1);
  not not_28 (not_28_out, Opcode1);
  not not_29 (not_29_out, Opcode2);
  not not_30 (not_30_out, Opcode1);
  not not_31 (not_31_out, Opcode2);
  not not_32 (not_32_out, Opcode1);
  not not_33 (not_33_out, Opcode3);
  not not_34 (not_34_out, Opcode1);
  and and_1 (and_1_out, not_1_out, not_2_out, not_3_out, not_4_out, not_5_out);
  and and_2 (and_2_out, not_6_out, not_7_out);
  and and_3 (and_3_out, not_8_out, not_9_out);
  and and_4 (and_4_out, not_10_out, Opcode0);
  and and_5 (and_5_out, Opcode2, not_11_out);
  and and_6 (and_6_out, Opcode4, not_12_out);
  and and_7 (and_7_out, Opcode5, not_13_out);
  and and_8 (and_8_out, not_14_out, not_15_out, Opcode3, not_16_out, not_17_out);
  and and_9 (Branch, not_18_out, Opcode2);
  and and_10 (and_10_out, Opcode3, not_19_out, Opcode0);
  and and_11 (and_11_out, Opcode3, not_20_out, Opcode1);
  and and_12 (and_12_out, Opcode4, Opcode3, not_21_out);
  and and_13 (and_13_out, Opcode5, Opcode3, not_22_out);
  and and_14 (and_14_out, not_23_out, not_24_out, not_25_out);
  and and_15 (and_15_out, not_26_out, not_27_out, Opcode0);
  and and_16 (and_16_out, Opcode3, Opcode2, not_28_out);
  and and_17 (and_17_out, Opcode4, not_29_out, not_30_out);
  and and_18 (and_18_out, Opcode5, not_31_out, not_32_out);
  and and_19 (ALUOp[0], not_33_out, Opcode2);
  and and_20 (isBne, not_34_out, Opcode0);
  or or_1 (RegWrite, and_1_out, and_2_out);
  or or_2 (RegDst, and_3_out, and_4_out, and_5_out, and_6_out, and_7_out);
  or or_3 (ALUSrc, Opcode1, and_8_out);
  or or_4 (MemWrite, and_10_out, and_11_out, and_12_out, and_13_out);
  or or_5 (ALUOp[1], and_14_out, and_15_out, and_16_out, and_17_out, and_18_out);

  assign MemtoReg = Opcode1;
endmodule

module \实验三控制单元  (
  input  [5:0] opcode,
  input  [5:0] funct,
  output RegWrite,
  output RegDst,
  output ALUSrc,
  output Branch,
  output MemWrite,
  output MemtoReg,
  output isBne,
  output [2:0] ALUControl,
  output Syscall
);

  wire [1:0] \实验三控制单元的主译码器_1_aluop ;

  \实验三控制单元的主译码器  \u_实验三控制单元的主译码器_1  (
    .Opcode5(opcode[5]), .Opcode4(opcode[4]), .Opcode3(opcode[3]), .Opcode2(opcode[2]), .Opcode1(opcode[1]),
    .Opcode0(opcode[0]), .RegWrite(RegWrite), .RegDst(RegDst), .ALUSrc(ALUSrc), .Branch(Branch),
    .MemWrite(MemWrite), .MemtoReg(MemtoReg), .ALUOp(\实验三控制单元的主译码器_1_aluop ), .isBne(isBne));
  \实验三ALU译码器  \u_实验三alu译码器_1  (.Funct(funct), .ALUOp(\实验三控制单元的主译码器_1_aluop ), .ALUControl(ALUControl));
  \实验三syscall控制元件  \u_实验三syscall控制元件_1  (
    .ALUOp1(\实验三控制单元的主译码器_1_aluop [1]), .ALUOp0(\实验三控制单元的主译码器_1_aluop [0]), .F5(funct[5]), .F4(funct[4]),
    .F3(funct[3]), .F2(funct[2]), .F1(funct[1]), .F0(funct[0]), .syscall(Syscall));
endmodule

module \实验三syscall控制元件  (
  input  ALUOp1,
  input  ALUOp0,
  input  F5,
  input  F4,
  input  F3,
  input  F2,
  input  F1,
  input  F0,
  output syscall
);

  wire not_1_out, not_2_out, not_3_out, not_4_out, not_5_out;

  not not_1 (not_1_out, ALUOp0);
  not not_2 (not_2_out, F5);
  not not_3 (not_3_out, F4);
  not not_4 (not_4_out, F1);
  not not_5 (not_5_out, F0);
  and and_1 (syscall, ALUOp1, not_1_out, not_2_out, not_3_out, F3, F2, not_4_out, not_5_out);
endmodule

module \实验三寄存器文件  (
  input  CLK,
  input  WE,
  input  [4:0] RA,
  input  [4:0] RC,
  input  [31:0] WD,
  input  [4:0] RB,
  output [31:0] RAD,
  output [31:0] RBD
);

  wire demultiplexer_1_out0, demultiplexer_1_out1, demultiplexer_1_out2, demultiplexer_1_out3,
       demultiplexer_1_out4, demultiplexer_1_out5, demultiplexer_1_out6, demultiplexer_1_out7,
       demultiplexer_1_out8, demultiplexer_1_out9, demultiplexer_1_out10, demultiplexer_1_out11,
       demultiplexer_1_out12, demultiplexer_1_out13, demultiplexer_1_out14, demultiplexer_1_out15,
       demultiplexer_1_out16, demultiplexer_1_out17, demultiplexer_1_out18, demultiplexer_1_out19,
       demultiplexer_1_out20, demultiplexer_1_out21, demultiplexer_1_out22, demultiplexer_1_out23,
       demultiplexer_1_out24, demultiplexer_1_out25, demultiplexer_1_out26, demultiplexer_1_out27,
       demultiplexer_1_out28, demultiplexer_1_out29, demultiplexer_1_out30, demultiplexer_1_out31;
  wire [31:0] register_1_q, register_2_q, register_3_q, register_4_q, register_5_q, register_6_q,
       register_7_q, register_8_q, register_9_q, register_10_q, register_11_q, register_12_q, register_13_q,
       register_14_q, register_15_q, register_17_q, register_18_q, register_19_q, register_20_q,
       register_21_q, register_22_q, register_23_q, register_24_q, register_25_q, register_26_q,
       register_27_q, register_28_q, register_29_q, register_30_q, register_31_q, register_32_q;

  Demultiplexer #(.select(5), .width(1), .tristate("false"), .disabled("Z"), .enable("false")) demultiplexer_1 (
    .out0(demultiplexer_1_out0), .out1(demultiplexer_1_out1), .out2(demultiplexer_1_out2),
    .out3(demultiplexer_1_out3), .out4(demultiplexer_1_out4), .out5(demultiplexer_1_out5),
    .out6(demultiplexer_1_out6), .out7(demultiplexer_1_out7), .out8(demultiplexer_1_out8),
    .out9(demultiplexer_1_out9), .out10(demultiplexer_1_out10), .out11(demultiplexer_1_out11),
    .out12(demultiplexer_1_out12), .out13(demultiplexer_1_out13), .out14(demultiplexer_1_out14),
    .out15(demultiplexer_1_out15), .out16(demultiplexer_1_out16), .out17(demultiplexer_1_out17),
    .out18(demultiplexer_1_out18), .out19(demultiplexer_1_out19), .out20(demultiplexer_1_out20),
    .out21(demultiplexer_1_out21), .out22(demultiplexer_1_out22), .out23(demultiplexer_1_out23),
    .out24(demultiplexer_1_out24), .out25(demultiplexer_1_out25), .out26(demultiplexer_1_out26),
    .out27(demultiplexer_1_out27), .out28(demultiplexer_1_out28), .out29(demultiplexer_1_out29),
    .out30(demultiplexer_1_out30), .out31(demultiplexer_1_out31), .in(WE), .sel(RC));
  Register #(.width(32), .trigger("rising"), .Select("low")) register_1 (
    .D(WD), .en(demultiplexer_1_out0), .Q(register_1_q), .clk(CLK));  // open: clr
  Register #(.width(32), .trigger("rising"), .Select("low")) register_2 (
    .D(WD), .en(demultiplexer_1_out1), .Q(register_2_q), .clk(CLK));  // open: clr
  Register #(.width(32), .trigger("rising"), .Select("low")) register_3 (
    .D(WD), .en(demultiplexer_1_out2), .Q(register_3_q), .clk(CLK));  // open: clr
  Register #(.width(32), .trigger("rising"), .Select("low")) register_4 (
    .D(WD), .en(demultiplexer_1_out3), .Q(register_4_q), .clk(CLK));  // open: clr
  Register #(.width(32), .trigger("rising"), .Select("low")) register_5 (
    .D(WD), .en(demultiplexer_1_out4), .Q(register_5_q), .clk(CLK));  // open: clr
  Register #(.width(32), .trigger("rising"), .Select("low")) register_6 (
    .D(WD), .en(demultiplexer_1_out5), .Q(register_6_q), .clk(CLK));  // open: clr
  Register #(.width(32), .trigger("rising"), .Select("low")) register_7 (
    .D(WD), .en(demultiplexer_1_out6), .Q(register_7_q), .clk(CLK));  // open: clr
  Register #(.width(32), .trigger("rising"), .Select("low")) register_8 (
    .D(WD), .en(demultiplexer_1_out7), .Q(register_8_q), .clk(CLK));  // open: clr
  Register #(.width(32), .trigger("rising"), .Select("low")) register_9 (
    .D(WD), .en(demultiplexer_1_out8), .Q(register_9_q), .clk(CLK));  // open: clr
  Register #(.width(32), .trigger("rising"), .Select("low")) register_10 (
    .D(WD), .en(demultiplexer_1_out9), .Q(register_10_q), .clk(CLK));  // open: clr
  Register #(.width(32), .trigger("rising"), .Select("low")) register_11 (
    .D(WD), .en(demultiplexer_1_out10), .Q(register_11_q), .clk(CLK));  // open: clr
  Register #(.width(32), .trigger("rising"), .Select("low")) register_12 (
    .D(WD), .en(demultiplexer_1_out11), .Q(register_12_q), .clk(CLK));  // open: clr
  Register #(.width(32), .trigger("rising"), .Select("low")) register_13 (
    .D(WD), .en(demultiplexer_1_out12), .Q(register_13_q), .clk(CLK));  // open: clr
  Register #(.width(32), .trigger("rising"), .Select("low")) register_14 (
    .D(WD), .en(demultiplexer_1_out13), .Q(register_14_q), .clk(CLK));  // open: clr
  Register #(.width(32), .trigger("rising"), .Select("low")) register_15 (
    .D(WD), .en(demultiplexer_1_out14), .Q(register_15_q), .clk(CLK));  // open: clr
  Register #(.width(32), .trigger("rising"), .Select("low")) register_16 (
    .D(WD), .en(demultiplexer_1_out15), .clk(CLK));  // open: Q, clr
  Register #(.width(32), .trigger("rising"), .Select("low")) register_17 (
    .D(WD), .en(demultiplexer_1_out16), .Q(register_17_q), .clk(CLK));  // open: clr
  Register #(.width(32), .trigger("rising"), .Select("low")) register_18 (
    .D(WD), .en(demultiplexer_1_out17), .Q(register_18_q), .clk(CLK));  // open: clr
  Register #(.width(32), .trigger("rising"), .Select("low")) register_19 (
    .D(WD), .en(demultiplexer_1_out18), .Q(register_19_q), .clk(CLK));  // open: clr
  Register #(.width(32), .trigger("rising"), .Select("low")) register_20 (
    .D(WD), .en(demultiplexer_1_out19), .Q(register_20_q), .clk(CLK));  // open: clr
  Register #(.width(32), .trigger("rising"), .Select("low")) register_21 (
    .D(WD), .en(demultiplexer_1_out20), .Q(register_21_q), .clk(CLK));  // open: clr
  Register #(.width(32), .trigger("rising"), .Select("low")) register_22 (
    .D(WD), .en(demultiplexer_1_out21), .Q(register_22_q), .clk(CLK));  // open: clr
  Register #(.width(32), .trigger("rising"), .Select("low")) register_23 (
    .D(WD), .en(demultiplexer_1_out22), .Q(register_23_q), .clk(CLK));  // open: clr
  Register #(.width(32), .trigger("rising"), .Select("low")) register_24 (
    .D(WD), .en(demultiplexer_1_out23), .Q(register_24_q), .clk(CLK));  // open: clr
  Register #(.width(32), .trigger("rising"), .Select("low")) register_25 (
    .D(WD), .en(demultiplexer_1_out24), .Q(register_25_q), .clk(CLK));  // open: clr
  Register #(.width(32), .trigger("rising"), .Select("low")) register_26 (
    .D(WD), .en(demultiplexer_1_out25), .Q(register_26_q), .clk(CLK));  // open: clr
  Register #(.width(32), .trigger("rising"), .Select("low")) register_27 (
    .D(WD), .en(demultiplexer_1_out26), .Q(register_27_q), .clk(CLK));  // open: clr
  Register #(.width(32), .trigger("rising"), .Select("low")) register_28 (
    .D(WD), .en(demultiplexer_1_out27), .Q(register_28_q), .clk(CLK));  // open: clr
  Register #(.width(32), .trigger("rising"), .Select("low")) register_29 (
    .D(WD), .en(demultiplexer_1_out28), .Q(register_29_q), .clk(CLK));  // open: clr
  Register #(.width(32), .trigger("rising"), .Select("low")) register_30 (
    .D(WD), .en(demultiplexer_1_out29), .Q(register_30_q), .clk(CLK));  // open: clr
  Register #(.width(32), .trigger("rising"), .Select("low")) register_31 (
    .D(WD), .en(demultiplexer_1_out30), .Q(register_31_q), .clk(CLK));  // open: clr
  Register #(.width(32), .trigger("rising"), .Select("low")) register_32 (
    .D(WD), .en(demultiplexer_1_out31), .Q(register_32_q), .clk(CLK));  // open: clr
  Multiplexer #(.select(5), .width(32), .disabled("Z"), .enable("false")) multiplexer_1 (
    .in0(register_1_q), .in1(register_2_q), .in2(register_3_q), .in3(register_4_q), .in4(register_5_q),
    .in5(register_6_q), .in6(register_7_q), .in7(register_8_q), .in8(register_9_q), .in9(register_10_q),
    .in10(register_11_q), .in11(register_12_q), .in12(register_13_q), .in13(register_14_q),
    .in14(register_15_q), .in15(register_1_q), .in16(register_17_q), .in17(register_18_q),
    .in18(register_19_q), .in19(register_20_q), .in20(register_21_q), .in21(register_22_q),
    .in22(register_23_q), .in23(register_24_q), .in24(register_25_q), .in25(register_26_q),
    .in26(register_27_q), .in27(register_28_q), .in28(register_29_q), .in29(register_30_q),
    .in30(register_31_q), .in31(register_32_q), .out(RAD), .sel(RA));
  Multiplexer #(.select(5), .width(32), .disabled("Z"), .enable("false")) multiplexer_2 (
    .in0(register_1_q), .in1(register_2_q), .in2(register_3_q), .in3(register_4_q), .in4(register_5_q),
    .in5(register_6_q), .in6(register_7_q), .in7(register_8_q), .in8(register_9_q), .in9(register_10_q),
    .in10(register_11_q), .in11(register_12_q), .in12(register_13_q), .in13(register_14_q),
    .in14(register_15_q), .in15(register_1_q), .in16(register_17_q), .in17(register_18_q),
    .in18(register_19_q), .in19(register_20_q), .in20(register_21_q), .in21(register_22_q),
    .in22(register_23_q), .in23(register_24_q), .in24(register_25_q), .in25(register_26_q),
    .in26(register_27_q), .in27(register_28_q), .in28(register_29_q), .in29(register_30_q),
    .in30(register_31_q), .in31(register_32_q), .out(RBD), .sel(RB));
endmodule

module \实验三寄存器文件的封装  (
  input  CLK,
  input  WE3,
  input  [4:0] A1,
  input  [4:0] A2,
  input  [4:0] A3,
  input  [31:0] WD3,
  output [31:0] RD1,
  output [31:0] RD2
);

  \实验三寄存器文件  \u_实验三寄存器文件_1  (.WE(WE3), .RC(A3), .WD(WD3), .CLK(CLK), .RA(A1), .RB(A2), .RAD(RD1), .RBD(RD2));
endmodule

module \实验三RAM  (
  input  CS,
  input  Store,
  input  CLK,
  input  [31:0] Address_Bus,
  input  [31:0] Data_Bus_In,
  input  Load,
  input  Clear,
  output [31:0] Data_Bus_Out
);

  wire decoder_1_out0, decoder_1_out1, decoder_1_out2, decoder_1_out3, decoder_1_out4, decoder_1_out5,
       decoder_1_out6, decoder_1_out7, decoder_2_out0, decoder_2_out1, decoder_2_out2, decoder_2_out3,
       decoder_2_out4, decoder_2_out5, decoder_2_out6, decoder_2_out7, nand_1_out, nand_2_out, nand_3_out,
       nand_4_out, nand_5_out, nand_6_out, nand_7_out, nand_8_out, nand_9_out, nand_10_out, nand_11_out,
       nand_12_out, nand_13_out, nand_14_out, nand_15_out, nand_16_out, nand_17_out, nand_18_out,
       nand_19_out, nand_20_out, nand_21_out, nand_22_out, nand_23_out, nand_24_out, nand_25_out,
       nand_26_out, nand_27_out, nand_28_out, nand_29_out, nand_30_out, nand_31_out, nand_32_out,
       nand_33_out, nand_34_out, nand_35_out, nand_36_out, nand_37_out, nand_38_out, nand_39_out,
       nand_40_out, nand_41_out, nand_42_out, nand_43_out, nand_44_out, nand_45_out, nand_46_out,
       nand_47_out, nand_48_out, nand_49_out, nand_50_out, nand_51_out, nand_52_out, nand_53_out,
       nand_54_out, nand_55_out, nand_56_out, nand_57_out, nand_58_out, nand_59_out, nand_60_out,
       nand_61_out, nand_62_out, nand_63_out, nand_64_out;

  Decoder #(.select(3), .tristate("false"), .disabled(0), .enable("true")) decoder_1 (
    .out0(decoder_1_out0), .out1(decoder_1_out1), .out2(decoder_1_out2), .out3(decoder_1_out3),
    .out4(decoder_1_out4), .out5(decoder_1_out5), .out6(decoder_1_out6), .out7(decoder_1_out7),
    .sel(Address_Bus[4:2]), .en(CS));
  Decoder #(.select(3), .tristate("false"), .disabled(0), .enable("true")) decoder_2 (
    .out0(decoder_2_out0), .out1(decoder_2_out1), .out2(decoder_2_out2), .out3(decoder_2_out3),
    .out4(decoder_2_out4), .out5(decoder_2_out5), .out6(decoder_2_out6), .out7(decoder_2_out7),
    .sel(Address_Bus[7:5]), .en(CS));
  nand nand_1 (nand_1_out, decoder_2_out0, decoder_1_out7);
  nand nand_2 (nand_2_out, decoder_2_out0, decoder_1_out6);
  nand nand_3 (nand_3_out, decoder_2_out0, decoder_1_out5);
  nand nand_4 (nand_4_out, decoder_2_out0, decoder_1_out4);
  nand nand_5 (nand_5_out, decoder_2_out0, decoder_1_out3);
  nand nand_6 (nand_6_out, decoder_2_out0, decoder_1_out2);
  nand nand_7 (nand_7_out, decoder_2_out0, decoder_1_out1);
  nand nand_8 (nand_8_out, decoder_2_out0, decoder_1_out0);
  RAM #(.addrWidth(24), .dataWidth(32), .bus("separate"), .Select("low")) ram_1 (
    .addr(Address_Bus[31:8]), .din(Data_Bus_In), .data(Data_Bus_Out), .str(Store), .sel(nand_1_out),
    .clk(CLK), .ld(Load), .clr(Clear));
  RAM #(.addrWidth(24), .dataWidth(32), .bus("separate"), .Select("low")) ram_2 (
    .addr(Address_Bus[31:8]), .din(Data_Bus_In), .data(Data_Bus_Out), .str(Store), .sel(nand_2_out),
    .clk(CLK), .ld(Load), .clr(Clear));
  RAM #(.addrWidth(24), .dataWidth(32), .bus("separate"), .Select("low")) ram_3 (
    .addr(Address_Bus[31:8]), .din(Data_Bus_In), .data(Data_Bus_Out), .str(Store), .sel(nand_3_out),
    .clk(CLK), .ld(Load), .clr(Clear));
  RAM #(.addrWidth(24), .dataWidth(32), .bus("separate"), .Select("low")) ram_4 (
    .addr(Address_Bus[31:8]), .din(Data_Bus_In), .data(Data_Bus_Out), .str(Store), .sel(nand_4_out),
    .clk(CLK), .ld(Load), .clr(Clear));
  RAM #(.addrWidth(24), .dataWidth(32), .bus("separate"), .Select("low")) ram_5 (
    .addr(Address_Bus[31:8]), .din(Data_Bus_In), .data(Data_Bus_Out), .str(Store), .sel(nand_5_out),
    .clk(CLK), .ld(Load), .clr(Clear));
  RAM #(.addrWidth(24), .dataWidth(32), .bus("separate"), .Select("low")) ram_6 (
    .addr(Address_Bus[31:8]), .din(Data_Bus_In), .data(Data_Bus_Out), .str(Store), .sel(nand_6_out),
    .clk(CLK), .ld(Load), .clr(Clear));
  RAM #(.addrWidth(24), .dataWidth(32), .bus("separate"), .Select("low")) ram_7 (
    .addr(Address_Bus[31:8]), .din(Data_Bus_In), .data(Data_Bus_Out), .str(Store), .sel(nand_7_out),
    .clk(CLK), .ld(Load), .clr(Clear));
  RAM #(.addrWidth(24), .dataWidth(32), .bus("separate"), .Select("low")) ram_8 (
    .addr(Address_Bus[31:8]), .din(Data_Bus_In), .data(Data_Bus_Out), .str(Store), .sel(nand_8_out),
    .clk(CLK), .ld(Load), .clr(Clear));
  nand nand_9 (nand_9_out, decoder_2_out1, decoder_1_out7);
  nand nand_10 (nand_10_out, decoder_2_out1, decoder_1_out6);
  nand nand_11 (nand_11_out, decoder_2_out1, decoder_1_out5);
  nand nand_12 (nand_12_out, decoder_2_out1, decoder_1_out4);
  nand nand_13 (nand_13_out, decoder_2_out1, decoder_1_out3);
  nand nand_14 (nand_14_out, decoder_2_out1, decoder_1_out2);
  nand nand_15 (nand_15_out, decoder_2_out1, decoder_1_out1);
  nand nand_16 (nand_16_out, decoder_2_out1, decoder_1_out0);
  RAM #(.addrWidth(24), .dataWidth(32), .bus("separate"), .Select("low")) ram_9 (
    .addr(Address_Bus[31:8]), .din(Data_Bus_In), .data(Data_Bus_Out), .str(Store), .sel(nand_9_out),
    .clk(CLK), .ld(Load), .clr(Clear));
  RAM #(.addrWidth(24), .dataWidth(32), .bus("separate"), .Select("low")) ram_10 (
    .addr(Address_Bus[31:8]), .din(Data_Bus_In), .data(Data_Bus_Out), .str(Store), .sel(nand_10_out),
    .clk(CLK), .ld(Load), .clr(Clear));
  RAM #(.addrWidth(24), .dataWidth(32), .bus("separate"), .Select("low")) ram_11 (
    .addr(Address_Bus[31:8]), .din(Data_Bus_In), .data(Data_Bus_Out), .str(Store), .sel(nand_11_out),
    .clk(CLK), .ld(Load), .clr(Clear));
  RAM #(.addrWidth(24), .dataWidth(32), .bus("separate"), .Select("low")) ram_12 (
    .addr(Address_Bus[31:8]), .din(Data_Bus_In), .data(Data_Bus_Out), .str(Store), .sel(nand_12_out),
    .clk(CLK), .ld(Load), .clr(Clear));
  RAM #(.addrWidth(24), .dataWidth(32), .bus("separate"), .Select("low")) ram_13 (
    .addr(Address_Bus[31:8]), .din(Data_Bus_In), .data(Data_Bus_Out), .str(Store), .sel(nand_13_out),
    .clk(CLK), .ld(Load), .clr(Clear));
  RAM #(.addrWidth(24), .dataWidth(32), .bus("separate"), .Select("low")) ram_14 (
    .addr(Address_Bus[31:8]), .din(Data_Bus_In), .data(Data_Bus_Out), .str(Store), .sel(nand_14_out),
    .clk(CLK), .ld(Load), .clr(Clear));
  RAM #(.addrWidth(24), .dataWidth(32), .bus("separate"), .Select("low")) ram_15 (
    .addr(Address_Bus[31:8]), .din(Data_Bus_In), .data(Data_Bus_Out), .str(Store), .sel(nand_15_out),
    .clk(CLK), .ld(Load), .clr(Clear));
  RAM #(.addrWidth(24), .dataWidth(32), .bus("separate"), .Select("low")) ram_16 (
    .addr(Address_Bus[31:8]), .din(Data_Bus_In), .data(Data_Bus_Out), .str(Store), .sel(nand_16_out),
    .clk(CLK), .ld(Load), .clr(Clear));
  nand nand_17 (nand_17_out, decoder_2_out2, decoder_1_out7);
  nand nand_18 (nand_18_out, decoder_2_out2, decoder_1_out6);
  nand nand_19 (nand_19_out, decoder_2_out2, decoder_1_out5);
  nand nand_20 (nand_20_out, decoder_2_out2, decoder_1_out4);
  nand nand_21 (nand_21_out, decoder_2_out2, decoder_1_out3);
  nand nand_22 (nand_22_out, decoder_2_out2, decoder_1_out2);
  nand nand_23 (nand_23_out, decoder_2_out2, decoder_1_out1);
  nand nand_24 (nand_24_out, decoder_2_out2, decoder_1_out0);
  RAM #(.addrWidth(24), .dataWidth(32), .bus("separate"), .Select("low")) ram_17 (
    .addr(Address_Bus[31:8]), .din(Data_Bus_In), .data(Data_Bus_Out), .str(Store), .sel(nand_17_out),
    .clk(CLK), .ld(Load), .clr(Clear));
  RAM #(.addrWidth(24), .dataWidth(32), .bus("separate"), .Select("low")) ram_18 (
    .addr(Address_Bus[31:8]), .din(Data_Bus_In), .data(Data_Bus_Out), .str(Store), .sel(nand_18_out),
    .clk(CLK), .ld(Load), .clr(Clear));
  RAM #(.addrWidth(24), .dataWidth(32), .bus("separate"), .Select("low")) ram_19 (
    .addr(Address_Bus[31:8]), .din(Data_Bus_In), .data(Data_Bus_Out), .str(Store), .sel(nand_19_out),
    .clk(CLK), .ld(Load), .clr(Clear));
  RAM #(.addrWidth(24), .dataWidth(32), .bus("separate"), .Select("low")) ram_20 (
    .addr(Address_Bus[31:8]), .din(Data_Bus_In), .data(Data_Bus_Out), .str(Store), .sel(nand_20_out),
    .clk(CLK), .ld(Load), .clr(Clear));
  RAM #(.addrWidth(24), .dataWidth(32), .bus("separate"), .Select("low")) ram_21 (
    .addr(Address_Bus[31:8]), .din(Data_Bus_In), .data(Data_Bus_Out), .str(Store), .sel(nand_21_out),
    .clk(CLK), .ld(Load), .clr(Clear));
  RAM #(.addrWidth(24), .dataWidth(32), .bus("separate"), .Select("low")) ram_22 (
    .addr(Address_Bus[31:8]), .din(Data_Bus_In), .data(Data_Bus_Out), .str(Store), .sel(nand_22_out),
    .clk(CLK), .ld(Load), .clr(Clear));
  RAM #(.addrWidth(24), .dataWidth(32), .bus("separate"), .Select("low")) ram_23 (
    .addr(Address_Bus[31:8]), .din(Data_Bus_In), .data(Data_Bus_Out), .str(Store), .sel(nand_23_out),
    .clk(CLK), .ld(Load), .clr(Clear));
  RAM #(.addrWidth(24), .dataWidth(32), .bus("separate"), .Select("low")) ram_24 (
    .addr(Address_Bus[31:8]), .din(Data_Bus_In), .data(Data_Bus_Out), .str(Store), .sel(nand_24_out),
    .clk(CLK), .ld(Load), .clr(Clear));
  nand nand_25 (nand_25_out, decoder_2_out3, decoder_1_out7);
  nand nand_26 (nand_26_out, decoder_2_out3, decoder_1_out6);
  nand nand_27 (nand_27_out, decoder_2_out3, decoder_1_out5);
  nand nand_28 (nand_28_out, decoder_2_out3, decoder_1_out4);
  nand nand_29 (nand_29_out, decoder_2_out3, decoder_1_out3);
  nand nand_30 (nand_30_out, decoder_2_out3, decoder_1_out2);
  nand nand_31 (nand_31_out, decoder_2_out3, decoder_1_out1);
  nand nand_32 (nand_32_out, decoder_2_out3, decoder_1_out0);
  RAM #(.addrWidth(24), .dataWidth(32), .bus("separate"), .Select("low")) ram_25 (
    .addr(Address_Bus[31:8]), .din(Data_Bus_In), .data(Data_Bus_Out), .str(Store), .sel(nand_25_out),
    .clk(CLK), .ld(Load), .clr(Clear));
  RAM #(.addrWidth(24), .dataWidth(32), .bus("separate"), .Select("low")) ram_26 (
    .addr(Address_Bus[31:8]), .din(Data_Bus_In), .data(Data_Bus_Out), .str(Store), .sel(nand_26_out),
    .clk(CLK), .ld(Load), .clr(Clear));
  RAM #(.addrWidth(24), .dataWidth(32), .bus("separate"), .Select("low")) ram_27 (
    .addr(Address_Bus[31:8]), .din(Data_Bus_In), .data(Data_Bus_Out), .str(Store), .sel(nand_27_out),
    .clk(CLK), .ld(Load), .clr(Clear));
  RAM #(.addrWidth(24), .dataWidth(32), .bus("separate"), .Select("low")) ram_28 (
    .addr(Address_Bus[31:8]), .din(Data_Bus_In), .data(Data_Bus_Out), .str(Store), .sel(nand_28_out),
    .clk(CLK), .ld(Load), .clr(Clear));
  RAM #(.addrWidth(24), .dataWidth(32), .bus("separate"), .Select("low")) ram_29 (
    .addr(Address_Bus[31:8]), .din(Data_Bus_In), .data(Data_Bus_Out), .str(Store), .sel(nand_29_out),
    .clk(CLK), .ld(Load), .clr(Clear));
  RAM #(.addrWidth(24), .dataWidth(32), .bus("separate"), .Select("low")) ram_30 (
    .addr(Address_Bus[31:8]), .din(Data_Bus_In), .data(Data_Bus_Out), .str(Store), .sel(nand_30_out),
    .clk(CLK), .ld(Load), .clr(Clear));
  RAM #(.addrWidth(24), .dataWidth(32), .bus("separate"), .Select("low")) ram_31 (
    .addr(Address_Bus[31:8]), .din(Data_Bus_In), .data(Data_Bus_Out), .str(Store), .sel(nand_31_out),
    .clk(CLK), .ld(Load), .clr(Clear));
  RAM #(.addrWidth(24), .dataWidth(32), .bus("separate"), .Select("low")) ram_32 (
    .addr(Address_Bus[31:8]), .din(Data_Bus_In), .data(Data_Bus_Out), .str(Store), .sel(nand_32_out),
    .clk(CLK), .ld(Load), .clr(Clear));
  nand nand_33 (nand_33_out, decoder_2_out4, decoder_1_out7);
  nand nand_34 (nand_34_out, decoder_2_out4, decoder_1_out6);
  nand nand_35 (nand_35_out, decoder_2_out4, decoder_1_out5);
  nand nand_36 (nand_36_out, decoder_2_out4, decoder_1_out4);
  nand nand_37 (nand_37_out, decoder_2_out4, decoder_1_out3);
  nand nand_38 (nand_38_out, decoder_2_out4, decoder_1_out2);
  nand nand_39 (nand_39_out, decoder_2_out4, decoder_1_out1);
  nand nand_40 (nand_40_out, decoder_2_out4, decoder_1_out0);
  RAM #(.addrWidth(24), .dataWidth(32), .bus("separate"), .Select("low")) ram_33 (
    .addr(Address_Bus[31:8]), .din(Data_Bus_In), .data(Data_Bus_Out), .str(Store), .sel(nand_33_out),
    .clk(CLK), .ld(Load), .clr(Clear));
  RAM #(.addrWidth(24), .dataWidth(32), .bus("separate"), .Select("low")) ram_34 (
    .addr(Address_Bus[31:8]), .din(Data_Bus_In), .data(Data_Bus_Out), .str(Store), .sel(nand_34_out),
    .clk(CLK), .ld(Load), .clr(Clear));
  RAM #(.addrWidth(24), .dataWidth(32), .bus("separate"), .Select("low")) ram_35 (
    .addr(Address_Bus[31:8]), .din(Data_Bus_In), .data(Data_Bus_Out), .str(Store), .sel(nand_35_out),
    .clk(CLK), .ld(Load), .clr(Clear));
  RAM #(.addrWidth(24), .dataWidth(32), .bus("separate"), .Select("low")) ram_36 (
    .addr(Address_Bus[31:8]), .din(Data_Bus_In), .data(Data_Bus_Out), .str(Store), .sel(nand_36_out),
    .clk(CLK), .ld(Load), .clr(Clear));
  RAM #(.addrWidth(24), .dataWidth(32), .bus("separate"), .Select("low")) ram_37 (
    .addr(Address_Bus[31:8]), .din(Data_Bus_In), .data(Data_Bus_Out), .str(Store), .sel(nand_37_out),
    .clk(CLK), .ld(Load), .clr(Clear));
  RAM #(.addrWidth(24), .dataWidth(32), .bus("separate"), .Select("low")) ram_38 (
    .addr(Address_Bus[31:8]), .din(Data_Bus_In), .data(Data_Bus_Out), .str(Store), .sel(nand_38_out),
    .clk(CLK), .ld(Load), .clr(Clear));
  RAM #(.addrWidth(24), .dataWidth(32), .bus("separate"), .Select("low")) ram_39 (
    .addr(Address_Bus[31:8]), .din(Data_Bus_In), .data(Data_Bus_Out), .str(Store), .sel(nand_39_out),
    .clk(CLK), .ld(Load), .clr(Clear));
  RAM #(.addrWidth(24), .dataWidth(32), .bus("separate"), .Select("low")) ram_40 (
    .addr(Address_Bus[31:8]), .din(Data_Bus_In), .data(Data_Bus_Out), .str(Store), .sel(nand_40_out),
    .clk(CLK), .ld(Load), .clr(Clear));
  nand nand_41 (nand_41_out, decoder_2_out5, decoder_1_out7);
  nand nand_42 (nand_42_out, decoder_2_out5, decoder_1_out6);
  nand nand_43 (nand_43_out, decoder_2_out5, decoder_1_out5);
  nand nand_44 (nand_44_out, decoder_2_out5, decoder_1_out4);
  nand nand_45 (nand_45_out, decoder_2_out5, decoder_1_out3);
  nand nand_46 (nand_46_out, decoder_2_out5, decoder_1_out2);
  nand nand_47 (nand_47_out, decoder_2_out5, decoder_1_out1);
  nand nand_48 (nand_48_out, decoder_2_out5, decoder_1_out0);
  RAM #(.addrWidth(24), .dataWidth(32), .bus("separate"), .Select("low")) ram_41 (
    .addr(Address_Bus[31:8]), .din(Data_Bus_In), .data(Data_Bus_Out), .str(Store), .sel(nand_41_out),
    .clk(CLK), .ld(Load), .clr(Clear));
  RAM #(.addrWidth(24), .dataWidth(32), .bus("separate"), .Select("low")) ram_42 (
    .addr(Address_Bus[31:8]), .din(Data_Bus_In), .data(Data_Bus_Out), .str(Store), .sel(nand_42_out),
    .clk(CLK), .ld(Load), .clr(Clear));
  RAM #(.addrWidth(24), .dataWidth(32), .bus("separate"), .Select("low")) ram_43 (
    .addr(Address_Bus[31:8]), .din(Data_Bus_In), .data(Data_Bus_Out), .str(Store), .sel(nand_43_out),
    .clk(CLK), .ld(Load), .clr(Clear));
  RAM #(.addrWidth(24), .dataWidth(32), .bus("separate"), .Select("low")) ram_44 (
    .addr(Address_Bus[31:8]), .din(Data_Bus_In), .data(Data_Bus_Out), .str(Store), .sel(nand_44_out),
    .clk(CLK), .ld(Load), .clr(Clear));
  RAM #(.addrWidth(24), .dataWidth(32), .bus("separate"), .Select("low")) ram_45 (
    .addr(Address_Bus[31:8]), .din(Data_Bus_In), .data(Data_Bus_Out), .str(Store), .sel(nand_45_out),
    .clk(CLK), .ld(Load), .clr(Clear));
  RAM #(.addrWidth(24), .dataWidth(32), .bus("separate"), .Select("low")) ram_46 (
    .addr(Address_Bus[31:8]), .din(Data_Bus_In), .data(Data_Bus_Out), .str(Store), .sel(nand_46_out),
    .clk(CLK), .ld(Load), .clr(Clear));
  RAM #(.addrWidth(24), .dataWidth(32), .bus("separate"), .Select("low")) ram_47 (
    .addr(Address_Bus[31:8]), .din(Data_Bus_In), .data(Data_Bus_Out), .str(Store), .sel(nand_47_out),
    .clk(CLK), .ld(Load), .clr(Clear));
  RAM #(.addrWidth(24), .dataWidth(32), .bus("separate"), .Select("low")) ram_48 (
    .addr(Address_Bus[31:8]), .din(Data_Bus_In), .data(Data_Bus_Out), .str(Store), .sel(nand_48_out),
    .clk(CLK), .ld(Load), .clr(Clear));
  nand nand_49 (nand_49_out, decoder_2_out6, decoder_1_out7);
  nand nand_50 (nand_50_out, decoder_2_out6, decoder_1_out6);
  nand nand_51 (nand_51_out, decoder_2_out6, decoder_1_out5);
  nand nand_52 (nand_52_out, decoder_2_out6, decoder_1_out4);
  nand nand_53 (nand_53_out, decoder_2_out6, decoder_1_out3);
  nand nand_54 (nand_54_out, decoder_2_out6, decoder_1_out2);
  nand nand_55 (nand_55_out, decoder_2_out6, decoder_1_out1);
  nand nand_56 (nand_56_out, decoder_2_out6, decoder_1_out0);
  RAM #(.addrWidth(24), .dataWidth(32), .bus("separate"), .Select("low")) ram_49 (
    .addr(Address_Bus[31:8]), .din(Data_Bus_In), .data(Data_Bus_Out), .str(Store), .sel(nand_49_out),
    .clk(CLK), .ld(Load), .clr(Clear));
  RAM #(.addrWidth(24), .dataWidth(32), .bus("separate"), .Select("low")) ram_50 (
    .addr(Address_Bus[31:8]), .din(Data_Bus_In), .data(Data_Bus_Out), .str(Store), .sel(nand_50_out),
    .clk(CLK), .ld(Load), .clr(Clear));
  RAM #(.addrWidth(24), .dataWidth(32), .bus("separate"), .Select("low")) ram_51 (
    .addr(Address_Bus[31:8]), .din(Data_Bus_In), .data(Data_Bus_Out), .str(Store), .sel(nand_51_out),
    .clk(CLK), .ld(Load), .clr(Clear));
  RAM #(.addrWidth(24), .dataWidth(32), .bus("separate"), .Select("low")) ram_52 (
    .addr(Address_Bus[31:8]), .din(Data_Bus_In), .data(Data_Bus_Out), .str(Store), .sel(nand_52_out),
    .clk(CLK), .ld(Load), .clr(Clear));
  RAM #(.addrWidth(24), .dataWidth(32), .bus("separate"), .Select("low")) ram_53 (
    .addr(Address_Bus[31:8]), .din(Data_Bus_In), .data(Data_Bus_Out), .str(Store), .sel(nand_53_out),
    .clk(CLK), .ld(Load), .clr(Clear));
  RAM #(.addrWidth(24), .dataWidth(32), .bus("separate"), .Select("low")) ram_54 (
    .addr(Address_Bus[31:8]), .din(Data_Bus_In), .data(Data_Bus_Out), .str(Store), .sel(nand_54_out),
    .clk(CLK), .ld(Load), .clr(Clear));
  RAM #(.addrWidth(24), .dataWidth(32), .bus("separate"), .Select("low")) ram_55 (
    .addr(Address_Bus[31:8]), .din(Data_Bus_In), .data(Data_Bus_Out), .str(Store), .sel(nand_55_out),
    .clk(CLK), .ld(Load), .clr(Clear));
  RAM #(.addrWidth(24), .dataWidth(32), .bus("separate"), .Select("low")) ram_56 (
    .addr(Address_Bus[31:8]), .din(Data_Bus_In), .data(Data_Bus_Out), .str(Store), .sel(nand_56_out),
    .clk(CLK), .ld(Load), .clr(Clear));
  nand nand_57 (nand_57_out, decoder_2_out7, decoder_1_out7);
  nand nand_58 (nand_58_out, decoder_2_out7, decoder_1_out6);
  nand nand_59 (nand_59_out, decoder_2_out7, decoder_1_out5);
  nand nand_60 (nand_60_out, decoder_2_out7, decoder_1_out4);
  nand nand_61 (nand_61_out, decoder_2_out7, decoder_1_out3);
  nand nand_62 (nand_62_out, decoder_2_out7, decoder_1_out2);
  nand nand_63 (nand_63_out, decoder_2_out7, decoder_1_out1);
  nand nand_64 (nand_64_out, decoder_2_out7, decoder_1_out0);
  RAM #(.addrWidth(24), .dataWidth(32), .bus("separate"), .Select("low")) ram_57 (
    .addr(Address_Bus[31:8]), .din(Data_Bus_In), .data(Data_Bus_Out), .str(Store), .sel(nand_57_out),
    .clk(CLK), .ld(Load), .clr(Clear));
  RAM #(.addrWidth(24), .dataWidth(32), .bus("separate"), .Select("low")) ram_58 (
    .addr(Address_Bus[31:8]), .din(Data_Bus_In), .data(Data_Bus_Out), .str(Store), .sel(nand_58_out),
    .clk(CLK), .ld(Load), .clr(Clear));
  RAM #(.addrWidth(24), .dataWidth(32), .bus("separate"), .Select("low")) ram_59 (
    .addr(Address_Bus[31:8]), .din(Data_Bus_In), .data(Data_Bus_Out), .str(Store), .sel(nand_59_out),
    .clk(CLK), .ld(Load), .clr(Clear));
  RAM #(.addrWidth(24), .dataWidth(32), .bus("separate"), .Select("low")) ram_60 (
    .addr(Address_Bus[31:8]), .din(Data_Bus_In), .data(Data_Bus_Out), .str(Store), .sel(nand_60_out),
    .clk(CLK), .ld(Load), .clr(Clear));
  RAM #(.addrWidth(24), .dataWidth(32), .bus("separate"), .Select("low")) ram_61 (
    .addr(Address_Bus[31:8]), .din(Data_Bus_In), .data(Data_Bus_Out), .str(Store), .sel(nand_61_out),
    .clk(CLK), .ld(Load), .clr(Clear));
  RAM #(.addrWidth(24), .dataWidth(32), .bus("separate"), .Select("low")) ram_62 (
    .addr(Address_Bus[31:8]), .din(Data_Bus_In), .data(Data_Bus_Out), .str(Store), .sel(nand_62_out),
    .clk(CLK), .ld(Load), .clr(Clear));
  RAM #(.addrWidth(24), .dataWidth(32), .bus("separate"), .Select("low")) ram_63 (
    .addr(Address_Bus[31:8]), .din(Data_Bus_In), .data(Data_Bus_Out), .str(Store), .sel(nand_63_out),
    .clk(CLK), .ld(Load), .clr(Clear));
  RAM #(.addrWidth(24), .dataWidth(32), .bus("separate"), .Select("low")) ram_64 (
    .addr(Address_Bus[31:8]), .din(Data_Bus_In), .data(Data_Bus_Out), .str(Store), .sel(nand_64_out),
    .clk(CLK), .ld(Load), .clr(Clear));

  // Other names for the same wires on the sheet: Ad_TP[31:0] = Address_Bus; Data_Bus_In_TP[31:0] = Data_Bus_In;
  //   DataOut[31:0] = Data_Bus_Out

  // Notes on the sheet:
  //   外部各接口定义与原RAM相同
  //   按照字节编址，但按照字对齐访问
endmodule

module \实验三ROM  (
  input  CS,
  input  [31:0] Address_Bus,
  output [31:0] Data_Bus_Out
);

  wire decoder_1_out0, decoder_1_out1, decoder_1_out2, decoder_1_out3, decoder_1_out4, decoder_1_out5,
       decoder_1_out6, decoder_1_out7, decoder_2_out0, decoder_2_out1, decoder_2_out2, decoder_2_out3,
       decoder_2_out4, decoder_2_out5, decoder_2_out6, decoder_2_out7, nand_1_out, nand_2_out, nand_3_out,
       nand_4_out, nand_5_out, nand_6_out, nand_7_out, nand_8_out, nand_9_out, nand_10_out, nand_11_out,
       nand_12_out, nand_13_out, nand_14_out, nand_15_out, nand_16_out, nand_17_out, nand_18_out,
       nand_19_out, nand_20_out, nand_21_out, nand_22_out, nand_23_out, nand_24_out, nand_25_out,
       nand_26_out, nand_27_out, nand_28_out, nand_29_out, nand_30_out, nand_31_out, nand_32_out,
       nand_33_out, nand_34_out, nand_35_out, nand_36_out, nand_37_out, nand_38_out, nand_39_out,
       nand_40_out, nand_41_out, nand_42_out, nand_43_out, nand_44_out, nand_45_out, nand_46_out,
       nand_47_out, nand_48_out, nand_49_out, nand_50_out, nand_51_out, nand_52_out, nand_53_out,
       nand_54_out, nand_55_out, nand_56_out, nand_57_out, nand_58_out, nand_59_out, nand_60_out,
       nand_61_out, nand_62_out, nand_63_out, nand_64_out;

  Decoder #(.select(3), .tristate("false"), .disabled(0), .enable("true")) decoder_1 (
    .out0(decoder_1_out0), .out1(decoder_1_out1), .out2(decoder_1_out2), .out3(decoder_1_out3),
    .out4(decoder_1_out4), .out5(decoder_1_out5), .out6(decoder_1_out6), .out7(decoder_1_out7),
    .sel(Address_Bus[4:2]), .en(CS));
  Decoder #(.select(3), .tristate("false"), .disabled(0), .enable("true")) decoder_2 (
    .out0(decoder_2_out0), .out1(decoder_2_out1), .out2(decoder_2_out2), .out3(decoder_2_out3),
    .out4(decoder_2_out4), .out5(decoder_2_out5), .out6(decoder_2_out6), .out7(decoder_2_out7),
    .sel(Address_Bus[7:5]), .en(CS));
  nand nand_1 (nand_1_out, decoder_2_out0, decoder_1_out7);
  nand nand_2 (nand_2_out, decoder_2_out0, decoder_1_out6);
  nand nand_3 (nand_3_out, decoder_2_out0, decoder_1_out5);
  nand nand_4 (nand_4_out, decoder_2_out0, decoder_1_out4);
  nand nand_5 (nand_5_out, decoder_2_out0, decoder_1_out3);
  nand nand_6 (nand_6_out, decoder_2_out0, decoder_1_out2);
  nand nand_7 (nand_7_out, decoder_2_out0, decoder_1_out1);
  nand nand_8 (nand_8_out, decoder_2_out0, decoder_1_out0);
  ROM #(.addrWidth(24), .dataWidth(32), .Select("low")) rom_1 (
    .addr(Address_Bus[31:8]), .data(Data_Bus_Out), .sel(nand_1_out));
  ROM #(.addrWidth(24), .dataWidth(32), .Select("low")) rom_2 (
    .addr(Address_Bus[31:8]), .data(Data_Bus_Out), .sel(nand_2_out));
  ROM #(.addrWidth(24), .dataWidth(32), .Select("low")) rom_3 (
    .addr(Address_Bus[31:8]), .data(Data_Bus_Out), .sel(nand_3_out));
  ROM #(.addrWidth(24), .dataWidth(32), .Select("low")) rom_4 (
    .addr(Address_Bus[31:8]), .data(Data_Bus_Out), .sel(nand_4_out));
  ROM #(.addrWidth(24), .dataWidth(32), .Select("low")) rom_5 (
    .addr(Address_Bus[31:8]), .data(Data_Bus_Out), .sel(nand_5_out));
  ROM #(.addrWidth(24), .dataWidth(32), .Select("low")) rom_6 (
    .addr(Address_Bus[31:8]), .data(Data_Bus_Out), .sel(nand_6_out));
  ROM #(.addrWidth(24), .dataWidth(32), .Select("low")) rom_7 (
    .addr(Address_Bus[31:8]), .data(Data_Bus_Out), .sel(nand_7_out));
  ROM #(.addrWidth(24), .dataWidth(32), .Select("low")) rom_8 (
    .addr(Address_Bus[31:8]), .data(Data_Bus_Out), .sel(nand_8_out));
  nand nand_9 (nand_9_out, decoder_2_out1, decoder_1_out7);
  nand nand_10 (nand_10_out, decoder_2_out1, decoder_1_out6);
  nand nand_11 (nand_11_out, decoder_2_out1, decoder_1_out5);
  nand nand_12 (nand_12_out, decoder_2_out1, decoder_1_out4);
  nand nand_13 (nand_13_out, decoder_2_out1, decoder_1_out3);
  nand nand_14 (nand_14_out, decoder_2_out1, decoder_1_out2);
  nand nand_15 (nand_15_out, decoder_2_out1, decoder_1_out1);
  nand nand_16 (nand_16_out, decoder_2_out1, decoder_1_out0);
  ROM #(.addrWidth(24), .dataWidth(32), .Select("low")) rom_9 (
    .addr(Address_Bus[31:8]), .data(Data_Bus_Out), .sel(nand_9_out));
  ROM #(.addrWidth(24), .dataWidth(32), .Select("low")) rom_10 (
    .addr(Address_Bus[31:8]), .data(Data_Bus_Out), .sel(nand_10_out));
  ROM #(.addrWidth(24), .dataWidth(32), .Select("low")) rom_11 (
    .addr(Address_Bus[31:8]), .data(Data_Bus_Out), .sel(nand_11_out));
  ROM #(.addrWidth(24), .dataWidth(32), .Select("low")) rom_12 (
    .addr(Address_Bus[31:8]), .data(Data_Bus_Out), .sel(nand_12_out));
  ROM #(.addrWidth(24), .dataWidth(32), .Select("low")) rom_13 (
    .addr(Address_Bus[31:8]), .data(Data_Bus_Out), .sel(nand_13_out));
  ROM #(.addrWidth(24), .dataWidth(32), .Select("low")) rom_14 (
    .addr(Address_Bus[31:8]), .data(Data_Bus_Out), .sel(nand_14_out));
  ROM #(.addrWidth(24), .dataWidth(32), .Select("low")) rom_15 (
    .addr(Address_Bus[31:8]), .data(Data_Bus_Out), .sel(nand_15_out));
  ROM #(.addrWidth(24), .dataWidth(32), .Select("low")) rom_16 (
    .addr(Address_Bus[31:8]), .data(Data_Bus_Out), .sel(nand_16_out));
  nand nand_17 (nand_17_out, decoder_2_out2, decoder_1_out7);
  nand nand_18 (nand_18_out, decoder_2_out2, decoder_1_out6);
  nand nand_19 (nand_19_out, decoder_2_out2, decoder_1_out5);
  nand nand_20 (nand_20_out, decoder_2_out2, decoder_1_out4);
  nand nand_21 (nand_21_out, decoder_2_out2, decoder_1_out3);
  nand nand_22 (nand_22_out, decoder_2_out2, decoder_1_out2);
  nand nand_23 (nand_23_out, decoder_2_out2, decoder_1_out1);
  nand nand_24 (nand_24_out, decoder_2_out2, decoder_1_out0);
  ROM #(.addrWidth(24), .dataWidth(32), .Select("low")) rom_17 (
    .addr(Address_Bus[31:8]), .data(Data_Bus_Out), .sel(nand_17_out));
  ROM #(.addrWidth(24), .dataWidth(32), .Select("low")) rom_18 (
    .addr(Address_Bus[31:8]), .data(Data_Bus_Out), .sel(nand_18_out));
  ROM #(.addrWidth(24), .dataWidth(32), .Select("low")) rom_19 (
    .addr(Address_Bus[31:8]), .data(Data_Bus_Out), .sel(nand_19_out));
  ROM #(.addrWidth(24), .dataWidth(32), .Select("low")) rom_20 (
    .addr(Address_Bus[31:8]), .data(Data_Bus_Out), .sel(nand_20_out));
  ROM #(.addrWidth(24), .dataWidth(32), .Select("low")) rom_21 (
    .addr(Address_Bus[31:8]), .data(Data_Bus_Out), .sel(nand_21_out));
  ROM #(.addrWidth(24), .dataWidth(32), .Select("low")) rom_22 (
    .addr(Address_Bus[31:8]), .data(Data_Bus_Out), .sel(nand_22_out));
  ROM #(.addrWidth(24), .dataWidth(32), .Select("low")) rom_23 (
    .addr(Address_Bus[31:8]), .data(Data_Bus_Out), .sel(nand_23_out));
  ROM #(.addrWidth(24), .dataWidth(32), .Select("low")) rom_24 (
    .addr(Address_Bus[31:8]), .data(Data_Bus_Out), .sel(nand_24_out));
  nand nand_25 (nand_25_out, decoder_2_out3, decoder_1_out7);
  nand nand_26 (nand_26_out, decoder_2_out3, decoder_1_out6);
  nand nand_27 (nand_27_out, decoder_2_out3, decoder_1_out5);
  nand nand_28 (nand_28_out, decoder_2_out3, decoder_1_out4);
  nand nand_29 (nand_29_out, decoder_2_out3, decoder_1_out3);
  nand nand_30 (nand_30_out, decoder_2_out3, decoder_1_out2);
  nand nand_31 (nand_31_out, decoder_2_out3, decoder_1_out1);
  nand nand_32 (nand_32_out, decoder_2_out3, decoder_1_out0);
  ROM #(.addrWidth(24), .dataWidth(32), .Select("low")) rom_25 (
    .addr(Address_Bus[31:8]), .data(Data_Bus_Out), .sel(nand_25_out));
  ROM #(.addrWidth(24), .dataWidth(32), .Select("low")) rom_26 (
    .addr(Address_Bus[31:8]), .data(Data_Bus_Out), .sel(nand_26_out));
  ROM #(.addrWidth(24), .dataWidth(32), .Select("low")) rom_27 (
    .addr(Address_Bus[31:8]), .data(Data_Bus_Out), .sel(nand_27_out));
  ROM #(.addrWidth(24), .dataWidth(32), .Select("low")) rom_28 (
    .addr(Address_Bus[31:8]), .data(Data_Bus_Out), .sel(nand_28_out));
  ROM #(.addrWidth(24), .dataWidth(32), .Select("low")) rom_29 (
    .addr(Address_Bus[31:8]), .data(Data_Bus_Out), .sel(nand_29_out));
  ROM #(.addrWidth(24), .dataWidth(32), .Select("low")) rom_30 (
    .addr(Address_Bus[31:8]), .data(Data_Bus_Out), .sel(nand_30_out));
  ROM #(.addrWidth(24), .dataWidth(32), .Select("low")) rom_31 (
    .addr(Address_Bus[31:8]), .data(Data_Bus_Out), .sel(nand_31_out));
  ROM #(.addrWidth(24), .dataWidth(32), .Select("low")) rom_32 (
    .addr(Address_Bus[31:8]), .data(Data_Bus_Out), .sel(nand_32_out));
  nand nand_33 (nand_33_out, decoder_2_out4, decoder_1_out7);
  nand nand_34 (nand_34_out, decoder_2_out4, decoder_1_out6);
  nand nand_35 (nand_35_out, decoder_2_out4, decoder_1_out5);
  nand nand_36 (nand_36_out, decoder_2_out4, decoder_1_out4);
  nand nand_37 (nand_37_out, decoder_2_out4, decoder_1_out3);
  nand nand_38 (nand_38_out, decoder_2_out4, decoder_1_out2);
  nand nand_39 (nand_39_out, decoder_2_out4, decoder_1_out1);
  nand nand_40 (nand_40_out, decoder_2_out4, decoder_1_out0);
  ROM #(.addrWidth(24), .dataWidth(32), .Select("low")) rom_33 (
    .addr(Address_Bus[31:8]), .data(Data_Bus_Out), .sel(nand_33_out));
  ROM #(.addrWidth(24), .dataWidth(32), .Select("low")) rom_34 (
    .addr(Address_Bus[31:8]), .data(Data_Bus_Out), .sel(nand_34_out));
  ROM #(.addrWidth(24), .dataWidth(32), .Select("low")) rom_35 (
    .addr(Address_Bus[31:8]), .data(Data_Bus_Out), .sel(nand_35_out));
  ROM #(.addrWidth(24), .dataWidth(32), .Select("low")) rom_36 (
    .addr(Address_Bus[31:8]), .data(Data_Bus_Out), .sel(nand_36_out));
  ROM #(.addrWidth(24), .dataWidth(32), .Select("low")) rom_37 (
    .addr(Address_Bus[31:8]), .data(Data_Bus_Out), .sel(nand_37_out));
  ROM #(.addrWidth(24), .dataWidth(32), .Select("low")) rom_38 (
    .addr(Address_Bus[31:8]), .data(Data_Bus_Out), .sel(nand_38_out));
  ROM #(.addrWidth(24), .dataWidth(32), .Select("low")) rom_39 (
    .addr(Address_Bus[31:8]), .data(Data_Bus_Out), .sel(nand_39_out));
  ROM #(.addrWidth(24), .dataWidth(32), .Select("low")) rom_40 (
    .addr(Address_Bus[31:8]), .data(Data_Bus_Out), .sel(nand_40_out));
  nand nand_41 (nand_41_out, decoder_2_out5, decoder_1_out7);
  nand nand_42 (nand_42_out, decoder_2_out5, decoder_1_out6);
  nand nand_43 (nand_43_out, decoder_2_out5, decoder_1_out5);
  nand nand_44 (nand_44_out, decoder_2_out5, decoder_1_out4);
  nand nand_45 (nand_45_out, decoder_2_out5, decoder_1_out3);
  nand nand_46 (nand_46_out, decoder_2_out5, decoder_1_out2);
  nand nand_47 (nand_47_out, decoder_2_out5, decoder_1_out1);
  nand nand_48 (nand_48_out, decoder_2_out5, decoder_1_out0);
  ROM #(.addrWidth(24), .dataWidth(32), .Select("low")) rom_41 (
    .addr(Address_Bus[31:8]), .data(Data_Bus_Out), .sel(nand_41_out));
  ROM #(.addrWidth(24), .dataWidth(32), .Select("low")) rom_42 (
    .addr(Address_Bus[31:8]), .data(Data_Bus_Out), .sel(nand_42_out));
  ROM #(.addrWidth(24), .dataWidth(32), .Select("low")) rom_43 (
    .addr(Address_Bus[31:8]), .data(Data_Bus_Out), .sel(nand_43_out));
  ROM #(.addrWidth(24), .dataWidth(32), .Select("low")) rom_44 (
    .addr(Address_Bus[31:8]), .data(Data_Bus_Out), .sel(nand_44_out));
  ROM #(.addrWidth(24), .dataWidth(32), .Select("low")) rom_45 (
    .addr(Address_Bus[31:8]), .data(Data_Bus_Out), .sel(nand_45_out));
  ROM #(.addrWidth(24), .dataWidth(32), .Select("low")) rom_46 (
    .addr(Address_Bus[31:8]), .data(Data_Bus_Out), .sel(nand_46_out));
  ROM #(.addrWidth(24), .dataWidth(32), .Select("low")) rom_47 (
    .addr(Address_Bus[31:8]), .data(Data_Bus_Out), .sel(nand_47_out));
  ROM #(.addrWidth(24), .dataWidth(32), .Select("low")) rom_48 (
    .addr(Address_Bus[31:8]), .data(Data_Bus_Out), .sel(nand_48_out));
  nand nand_49 (nand_49_out, decoder_2_out6, decoder_1_out7);
  nand nand_50 (nand_50_out, decoder_2_out6, decoder_1_out6);
  nand nand_51 (nand_51_out, decoder_2_out6, decoder_1_out5);
  nand nand_52 (nand_52_out, decoder_2_out6, decoder_1_out4);
  nand nand_53 (nand_53_out, decoder_2_out6, decoder_1_out3);
  nand nand_54 (nand_54_out, decoder_2_out6, decoder_1_out2);
  nand nand_55 (nand_55_out, decoder_2_out6, decoder_1_out1);
  nand nand_56 (nand_56_out, decoder_2_out6, decoder_1_out0);
  ROM #(.addrWidth(24), .dataWidth(32), .Select("low")) rom_49 (
    .addr(Address_Bus[31:8]), .data(Data_Bus_Out), .sel(nand_49_out));
  ROM #(.addrWidth(24), .dataWidth(32), .Select("low")) rom_50 (
    .addr(Address_Bus[31:8]), .data(Data_Bus_Out), .sel(nand_50_out));
  ROM #(.addrWidth(24), .dataWidth(32), .Select("low")) rom_51 (
    .addr(Address_Bus[31:8]), .data(Data_Bus_Out), .sel(nand_51_out));
  ROM #(.addrWidth(24), .dataWidth(32), .Select("low")) rom_52 (
    .addr(Address_Bus[31:8]), .data(Data_Bus_Out), .sel(nand_52_out));
  ROM #(.addrWidth(24), .dataWidth(32), .Select("low")) rom_53 (
    .addr(Address_Bus[31:8]), .data(Data_Bus_Out), .sel(nand_53_out));
  ROM #(.addrWidth(24), .dataWidth(32), .Select("low")) rom_54 (
    .addr(Address_Bus[31:8]), .data(Data_Bus_Out), .sel(nand_54_out));
  ROM #(.addrWidth(24), .dataWidth(32), .Select("low")) rom_55 (
    .addr(Address_Bus[31:8]), .data(Data_Bus_Out), .sel(nand_55_out));
  ROM #(.addrWidth(24), .dataWidth(32), .Select("low")) rom_56 (
    .addr(Address_Bus[31:8]), .data(Data_Bus_Out), .sel(nand_56_out));
  nand nand_57 (nand_57_out, decoder_2_out7, decoder_1_out7);
  nand nand_58 (nand_58_out, decoder_2_out7, decoder_1_out6);
  nand nand_59 (nand_59_out, decoder_2_out7, decoder_1_out5);
  nand nand_60 (nand_60_out, decoder_2_out7, decoder_1_out4);
  nand nand_61 (nand_61_out, decoder_2_out7, decoder_1_out3);
  nand nand_62 (nand_62_out, decoder_2_out7, decoder_1_out2);
  nand nand_63 (nand_63_out, decoder_2_out7, decoder_1_out1);
  nand nand_64 (nand_64_out, decoder_2_out7, decoder_1_out0);
  ROM #(.addrWidth(24), .dataWidth(32), .Select("low")) rom_57 (
    .addr(Address_Bus[31:8]), .data(Data_Bus_Out), .sel(nand_57_out));
  ROM #(.addrWidth(24), .dataWidth(32), .Select("low")) rom_58 (
    .addr(Address_Bus[31:8]), .data(Data_Bus_Out), .sel(nand_58_out));
  ROM #(.addrWidth(24), .dataWidth(32), .Select("low")) rom_59 (
    .addr(Address_Bus[31:8]), .data(Data_Bus_Out), .sel(nand_59_out));
  ROM #(.addrWidth(24), .dataWidth(32), .Select("low")) rom_60 (
    .addr(Address_Bus[31:8]), .data(Data_Bus_Out), .sel(nand_60_out));
  ROM #(.addrWidth(24), .dataWidth(32), .Select("low")) rom_61 (
    .addr(Address_Bus[31:8]), .data(Data_Bus_Out), .sel(nand_61_out));
  ROM #(.addrWidth(24), .dataWidth(32), .Select("low")) rom_62 (
    .addr(Address_Bus[31:8]), .data(Data_Bus_Out), .sel(nand_62_out));
  ROM #(.addrWidth(24), .dataWidth(32), .Select("low")) rom_63 (
    .addr(Address_Bus[31:8]), .data(Data_Bus_Out), .sel(nand_63_out));
  ROM #(.addrWidth(24), .dataWidth(32), .Select("low")) rom_64 (
    .addr(Address_Bus[31:8]), .data(Data_Bus_Out), .sel(nand_64_out));

  // Other names for the same wires on the sheet: Ad_TP[31:0] = Address_Bus; DataOut[31:0] = Data_Bus_Out

  // Notes on the sheet:
  //   外部各接口定义与原ROM相同
  //   按照字节编址，但按照字对齐访问
endmodule
